# Fritzing sketch RPI (saved by Fritzing 0.9.3b)
breadboards: 1

parts:
  LCD1 = LCD screen  # not connected
  U1 = 7-SEGMENT-4DIGIT [package=7-segment-4digit-youngsun]
  R1 = Resistor [tolerance=±5% resistance=100 package=THT]
  R2 = Resistor [tolerance=±5% resistance=100 package=THT]
  R3 = Resistor [tolerance=±5% resistance=100 package=THT]
  R4 = Resistor [tolerance=±5% resistance=100 package=THT]
  R5 = Resistor [tolerance=±5% resistance=100 package=THT]
  R6 = Resistor [tolerance=±5% resistance=100 package=THT]
  R7 = Resistor [tolerance=±5% resistance=100 package=THT]
  R8 = Resistor [tolerance=±5% resistance=100 package=THT]
  Raspberry_Pi_1 = Raspberry Pi 3 [part_number=RPI-3-V1.2]
  LED1 = RGB LED (com. cathode, rbg) [package="5 mm [THT]"]
  R9 = Resistor [tolerance=±5% resistance=150 package=THT]
  R10 = Resistor [tolerance=±5% resistance=100 package=THT]
  R11 = Resistor [tolerance=±5% resistance=100 package=THT]
  J1 = Piezo Speaker

nets:
  N1: U1.1, R1.Pin_1
  N2: U1.2, R2.Pin_1
  N3: U1.3, R3.Pin_1
  N4: U1.4, Raspberry_Pi_1.GIPO12
  N5: U1.5, R4.Pin_0
  N6: U1.6, R5.Pin_0
  N7: U1.9, R8.Pin_0
  N8: U1.11, Raspberry_Pi_1.GIPO27
  N9: U1.13, Raspberry_Pi_1.GIPO22
  N10: U1.14, R7.Pin_1
  N11: U1.15, R6.Pin_1
  N12: U1.16, Raspberry_Pi_1.GIPO5
  N13: R1.Pin_0, Raspberry_Pi_1.GIPO21
  N14: R2.Pin_0, Raspberry_Pi_1.GIPO20
  N15: R3.Pin_0, Raspberry_Pi_1.GIPO16
  N16: R4.Pin_1, Raspberry_Pi_1.GIPO25
  N17: R5.Pin_1, Raspberry_Pi_1.GIPO24
  N18: R6.Pin_0, Raspberry_Pi_1.GIPO6
  N19: R7.Pin_0, Raspberry_Pi_1.GIPO13
  N20: R8.Pin_1, Raspberry_Pi_1.GIPO4
  N21: Raspberry_Pi_1.GIPO11, J1.pin2
  N22: Raspberry_Pi_1.GIPO19, R10.Pin_0
  N23: Raspberry_Pi_1.GIPO26, R11.Pin_0
  N24: Raspberry_Pi_1.GIPO23, R9.Pin_0
  N25: LED1.red_anode, R9.Pin_1
  N26: LED1.common_cathode, J1.pin1
  N27: LED1.blue_anode, R10.Pin_1
  N28: LED1.green_anode, R11.Pin_1
